# Fritzing sketch 实验七 (saved by Fritzing 0.9.10b)
breadboards: 2

parts:
  74HC1 = 74HC20 - Dual 4-input NAND gate [package="DIP (Dual Inline) [THT]"]
  74HC2 = 74HC00 - Quad 2-input NAND gate [package="DIP (Dual Inline) [THT]"]
  74HC3 = 74HC74 - Dual D-type flip-flop with set andreset; positive-edge trigger [package="DIP (Dual Inline) [THT]"]
  74HC4 = 74HC74 - Dual D-type flip-flop with set andreset; positive-edge trigger [package="DIP (Dual Inline) [THT]"]
  74HC5 = 74HC86 - Quad 2-input EXCLUSIVE-OR gate [package="DIP (Dual Inline) [THT]"]

nets:
  VCC: 74HC1.1A, 74HC1.2A, 74HC1.Vcc, 74HC2.1A, 74HC2.Vcc, 74HC3.1S(bar)D, 74HC3.2S(bar)D, 74HC3.Vcc, 74HC4.1S(bar)D, 74HC4.Vcc, 74HC5.Vcc
  N1: 74HC1.1B, 74HC1.2C, 74HC2.3B, 74HC3.2Q(bar)
  N2: 74HC1.1C, 74HC3.1Q(bar)
  N3: 74HC1.1D, 74HC4.1Q(bar)
  N4: 74HC1.pin61Y, 74HC2.1B
  GND: 74HC1.GND, 74HC2.GND, 74HC3.GND, 74HC4.GND, 74HC5.GND
  N5: 74HC1.2Y, 74HC2.2B, 74HC2.3A, 74HC5.4B
  N6: 74HC1.2B, 74HC4.1Q, 74HC5.2B
  N7: 74HC1.2D, 74HC2.4A, 74HC3.1Q, 74HC5.1B
  N8: 74HC2.2A, 74HC2.4Y
  N9: 74HC2.2Y, 74HC5.2A
  N10: 74HC2.3Y, 74HC5.1A
  N11: 74HC2.4B, 74HC3.2Q, 74HC5.4A
  N12: 74HC3.1R(bar)D, 74HC3.2R(bar)D, 74HC4.1R(bar)D
  N13: 74HC3.1D, 74HC5.1Y
  N14: 74HC3.1CP, 74HC3.2CP, 74HC4.1CP
  N15: 74HC3.2D, 74HC5.4Y
  N16: 74HC4.1D, 74HC5.2Y

notes:
  Reset
  Clk

custom parts:
  74HC20 - Dual 4-input NAND gate: The 74HC/HCT20 are high-speed Si-gate CMOS devices and are pin compatible with low power Schottky TTL (LSTTL).They are specified in compliance with JEDEC standard no. 7A. The 74HC/HCT20 provide the 4-input NAND function.
  74HC00 - Quad 2-input NAND gate: The 74HC00; 74HCT00 are high-speed Si-gate CMOS devices that comply with JEDEC standard no. 7A. They are pin compatible with Low-power Schottky TTL (LSTTL).The 74HC00; 74HCT00 provides a quad 2-input NAND function.
  74HC74 - Dual D-type flip-flop with set andreset; positive-edge trigger: The 74HC/HCT74 is a high-speed Si-gate CMOS deviceand is pin compatible with low power Schottky TTL(LSTTL). They are specified in compliance with JEDECstandard no. 7A.
  74HC86 - Quad 2-input EXCLUSIVE-OR gate: The 74HC/HCT86 are high-speed Si-gate CMOS devicesand are pin compatible with low power Schottky TTL(LSTTL). They are specified in compliance with JEDECstandard no. 7A.The 74HC/HCT86 provide the EXCLUSIVE−OR function.
